# Fritzing sketch EggIncubatorSketch (saved by Fritzing 0.9.4)
breadboards: 1

parts:
  TEMP_HUM = DHT22 Humidity and Temperature Sensor
  Part1 = Arduino Uno (Rev3)
  FAN = DC Motor
  SERVO = Basic Servo
  V1 = DC Power [voltage=220]
  BULB = Resistor [tolerance=±5% resistance=100k package=THT]
  V3 = DC Power [voltage=12V]
  PULLUP_RES = Resistor [tolerance=±5% resistance=4.5k package=THT]
  LCD = LCD screen 16x2 IIC [part_number=101290]
  PT100 = Resistor [tolerance=±5% resistance=220 package="2010 [SMD]"]  # not connected
  Q1 = TRANSISTOR_NPN [package=to-92-ammo]
  R1 = Resistor [tolerance=±5% resistance=1k package="1206 [SMD]"]
  RELAY = KY-019 5V Relay Module [package="Breakout board"]
  R2 = Resistor [tolerance=±5% resistance=220 package=THT]  # not connected
  Water_Pump = DC Motor
  Water_Level_Sensor1 = Water Level Sensor
  Motor_Driver = L293D [package=THT]
  R3 = Temperature Sensor (Thermistor) [thermistor_type=NTC package=THT]
  10k_ntc = Resistor [tolerance=±5% resistance=220 package=THT]

nets:
  VCC: TEMP_HUM.VDD, Part1.5V, SERVO.vcc, PULLUP_RES.Pin_0, LCD.VCC, RELAY.+, Water_Level_Sensor1.VCC, R3.pin_0
  N1: TEMP_HUM.DATA, Part1.D4, PULLUP_RES.Pin_1
  GND: TEMP_HUM.GND, Part1.GND, SERVO.gnd, Water_Level_Sensor1.GND
  N2: Part1.A0, R3.pin_1, 10k_ntc.Pin_0
  N3: Part1.A3, Water_Level_Sensor1.SIG
  N4: Part1.A4/SDA, LCD.SDA
  N5: Part1.D8, Motor_Driver.In_1
  N6: Part1.D10_PWM/SS, Motor_Driver.In_2
  N7: Part1.A5/SCL, LCD.SCL
  N8: Part1.D2, RELAY.S
  N9: Part1.D3_PWM, SERVO.pulse
  N10: Part1.D5_PWM, Motor_Driver.Enable_1
  N11: Part1.D7, R1.Pin_0
  N12: FAN.pin_1, V3.V+, Motor_Driver.+Vmotor
  N13: FAN.pin_2, Q1.C
  N14: V1.V+, RELAY.NC
  GND_2: V1.V-, BULB.Pin_1, V3.V-, LCD.GND, Q1.E, RELAY.-, Motor_Driver.0V, 10k_ntc.Pin_1
  N15: BULB.Pin_0, RELAY.Common
  N16: Q1.B, R1.Pin_1
  N17: Water_Pump.pin_1, Motor_Driver.Out_1_(_Controlled_by_Enable_1_)
  N18: Water_Pump.pin_2, Motor_Driver.Out_2_(_Controlled_by_Enable_1_)

custom parts:
  LCD screen 16x2 IIC: LCD screen with HD44780 controller enables showing text, symbols, value or anything else that comes from Croduino/Arduino. It is capable of showing 16 symbols in two lines and therefore can be used in many projects that need to send clearly visible and legible output information.. • Color of symbols: White • Backlight: Blue • Dimensions: 80 x 36 x 12 mm • Screen dimensions: 64.5 x 16 mm •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
  KY-019 5V Relay Module: KY-019 5V Relay module, used to control AC circuits.
  Water Level Sensor: A water level sensor. This sensor operates at 3V to 5V. The Sig (signal) pin outputs an analogue signal that is in proportion to the amount of water in contact with the sensor.
