# Fritzing sketch Kuluçka makinesi v1 (saved by Fritzing 0.9.4)
breadboards: 1

parts:
  TEMP_HUM = DHT22 Humidity and Temperature Sensor
  Part1 = Arduino Uno (Rev3)
  FAN = DC Motor
  SERVO = Basic Servo
  V1 = DC Power [voltage=220]
  BULB = Resistor [tolerance=±5% resistance=100k package=THT]
  RELAY = songle relay
  MOSFET_FAN = MOSFET-NCHANNEL [package=to220v]
  V3 = DC Power [voltage=12V]
  PULLUP_RES = Resistor [tolerance=±5% resistance=30k package=THT]
  U1 = LCD-16X2 [package=lcd-8x2]  # not connected

nets:
  VDD: TEMP_HUM.VDD, Part1.5V, SERVO.vcc, PULLUP_RES.Pin_0
  N1: TEMP_HUM.DATA, Part1.D4, PULLUP_RES.Pin_1
  GND: TEMP_HUM.GND, Part1.GND, SERVO.gnd
  N2: Part1.D2, RELAY.VCC
  N3: Part1.D3_PWM, SERVO.pulse
  N4: Part1.D7, MOSFET_FAN.G
  N5: FAN.pin_1, V3.V+
  N6: FAN.pin_2, MOSFET_FAN.D
  N7: V1.V+, BULB.Pin_0
  GND_2: V1.V-, RELAY.NO, RELAY.GND, MOSFET_FAN.S, V3.V-
  N8: BULB.Pin_1, RELAY.COMMON
