# Fritzing sketch Kuluçka makinesi v2 (saved by Fritzing 0.9.4)
breadboards: 1

parts:
  TEMP_HUM = DHT22 Humidity and Temperature Sensor
  Part1 = Arduino Uno (Rev3)
  FAN = DC Motor
  SERVO = Basic Servo
  V1 = DC Power [voltage=220]
  BULB = Resistor [tolerance=±5% resistance=100k package=THT]
  RELAY = songle relay
  MOSFET_FAN = MOSFET-NCHANNEL [package=to220v]
  V3 = DC Power [voltage=12V]
  PULLUP_RES = Resistor [tolerance=±5% resistance=30k package=THT]
  Display1 = LCD screen 16x2 IIC [part_number=101290]
  PT100 = Resistor [tolerance=±5% resistance=220 package="2010 [SMD]"]  # not connected

nets:
  VCC: TEMP_HUM.VDD, Part1.5V, SERVO.vcc, PULLUP_RES.Pin_0, Display1.VCC
  N1: TEMP_HUM.DATA, Part1.D4, PULLUP_RES.Pin_1
  GND: TEMP_HUM.GND, Part1.GND, SERVO.gnd
  N2: Part1.A4/SDA, Display1.SDA
  N3: Part1.A5/SCL, Display1.SCL
  N4: Part1.D2, RELAY.VCC
  N5: Part1.D3_PWM, SERVO.pulse
  N6: Part1.D7, MOSFET_FAN.G
  N7: FAN.pin_1, V3.V+
  N8: FAN.pin_2, MOSFET_FAN.D
  N9: V1.V+, BULB.Pin_0
  GND_2: V1.V-, RELAY.NO, RELAY.GND, MOSFET_FAN.S, V3.V-, Display1.GND
  N10: BULB.Pin_1, RELAY.COMMON

custom parts:
  LCD screen 16x2 IIC: LCD screen with HD44780 controller enables showing text, symbols, value or anything else that comes from Croduino/Arduino. It is capable of showing 16 symbols in two lines and therefore can be used in many projects that need to send clearly visible and legible output information.. • Color of symbols: White • Backlight: Blue • Dimensions: 80 x 36 x 12 mm • Screen dimensions: 64.5 x 16 mm •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
