# Fritzing sketch Kuluçka makinesi v4 +base resistor (saved by Fritzing 0.9.4)
breadboards: 1

parts:
  TEMP_HUM = DHT22 Humidity and Temperature Sensor
  Part1 = Arduino Uno (Rev3)
  FAN = DC Motor
  SERVO = Basic Servo
  V1 = DC Power [voltage=220]
  BULB = Resistor [tolerance=±5% resistance=100k package=THT]
  RELAY = songle relay
  V3 = DC Power [voltage=12V]
  PULLUP_RES = Resistor [tolerance=±5% resistance=4.5k package=THT]
  Display1 = LCD screen 16x2 IIC [part_number=101290]
  PT100 = Resistor [tolerance=±5% resistance=220 package="2010 [SMD]"]  # not connected
  Q1 = TRANSISTOR_NPN [package=to-92-ammo]
  R1 = Resistor [tolerance=±5% resistance=1k package="1206 [SMD]"]

nets:
  VCC: TEMP_HUM.VDD, Part1.5V, SERVO.vcc, PULLUP_RES.Pin_0, Display1.VCC
  N1: TEMP_HUM.DATA, Part1.D4, PULLUP_RES.Pin_1
  GND: TEMP_HUM.GND, Part1.GND, SERVO.gnd
  N2: Part1.A4/SDA, Display1.SDA
  N3: Part1.A5/SCL, Display1.SCL
  N4: Part1.D2, RELAY.VCC
  N5: Part1.D3_PWM, SERVO.pulse
  N6: Part1.D7, R1.Pin_0
  N7: FAN.pin_1, V3.V+
  N8: FAN.pin_2, Q1.C
  N9: V1.V+, BULB.Pin_0
  GND_2: V1.V-, RELAY.NO, RELAY.GND, V3.V-, Display1.GND, Q1.E
  N10: BULB.Pin_1, RELAY.COMMON
  N11: Q1.B, R1.Pin_1

custom parts:
  LCD screen 16x2 IIC: LCD screen with HD44780 controller enables showing text, symbols, value or anything else that comes from Croduino/Arduino. It is capable of showing 16 symbols in two lines and therefore can be used in many projects that need to send clearly visible and legible output information.. • Color of symbols: White • Backlight: Blue • Dimensions: 80 x 36 x 12 mm • Screen dimensions: 64.5 x 16 mm •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
